// Logisim project 4-bit_ALU.circ as structural Verilog: 3 circuits, main circuit main
// 4-bit ALU
module main (
  input  [3:0] A,
  input  [3:0] B,
  input  [3:0] opcode,
  output overflow,
  output carry,
  output zero,
  output negative,
  output [3:0] Y
);

  wire [3:0] au_1_y, lu_1_y, multiplexer_1_out, not_1_out;

  assign not_1_out = ~B;  // NOT_Gate not_1, 4 bits wide
  Multiplexer #(.width(4), .disabled(0), .enable("false")) multiplexer_1 (
    .in0(B), .in1(not_1_out), .out(multiplexer_1_out), .sel(opcode[0]));
  AU au_1 (.A(A), .B(multiplexer_1_out), .cin(opcode[0]), .cout(carry), .overflow(overflow), .Y(au_1_y));
  LU lu_1 (.A(A), .Y(lu_1_y), .B(multiplexer_1_out), .f0(opcode[0]));
  Multiplexer #(.width(4), .disabled(0), .enable("false")) multiplexer_2 (
    .in0(au_1_y), .in1(lu_1_y), .out({negative, Y[2:0]}), .sel(opcode[1]));
  nor nor_1 (zero, Y[0], Y[1], Y[2], negative);

  assign Y[3] = negative;

  // Notes on the sheet:
  //   00 -> ADD
  //   01 ->SUB
  //   10 -> AND
  //   11 -> OR
  //   Rafat Hasan - 1731117
endmodule

module AU (
  input  cin,
  input  [3:0] A,
  input  [3:0] B,
  output [3:0] Y,
  output cout,
  output overflow
);

  wire adder_1_cout, adder_2_cout, adder_3_cout;

  Adder #(.width(1)) adder_1 (.a(A[0]), .b(B[0]), .out(Y[0]), .cin(cin), .cout(adder_1_cout));
  Adder #(.width(1)) adder_2 (.a(A[1]), .b(B[1]), .out(Y[1]), .cin(adder_1_cout), .cout(adder_2_cout));
  Adder #(.width(1)) adder_3 (.a(A[2]), .b(B[2]), .out(Y[2]), .cin(adder_2_cout), .cout(adder_3_cout));
  Adder #(.width(1)) adder_4 (.a(A[3]), .b(B[3]), .out(Y[3]), .cin(adder_3_cout), .cout(cout));
  xor xor_1 (overflow, adder_3_cout, cout);
endmodule

module LU (
  input  [3:0] A,
  input  [3:0] B,
  input  f0,
  output [3:0] Y
);

  wire [3:0] and_1_out, or_1_out;

  assign and_1_out = A & B;  // AND_Gate and_1, 4 bits wide
  assign or_1_out = A | B;  // OR_Gate or_1, 4 bits wide
  Multiplexer #(.width(4), .disabled(0), .enable("false")) multiplexer_1 (
    .in0(and_1_out), .in1(or_1_out), .out(Y), .sel(f0));
endmodule
